# Fritzing sketch schematic (saved by Fritzing 0.9.3b)
breadboards: 1

parts:
  DFRobot_DFPlayer_Mini1 = DFRobot DFPlayer Mini [part_number=DFR0299]
  SP1 = SPEAKER [package=pcb_mount_speaker]
  S1 = Round Pushbutton
  VCC1 = Battery

nets:
  N1: DFRobot_DFPlayer_Mini1.VCC, VCC1.+
  N2: DFRobot_DFPlayer_Mini1.SPK_1, SP1.-
  N3: DFRobot_DFPlayer_Mini1.GND-1, DFRobot_DFPlayer_Mini1.GND-2, S1.leg0
  N4: DFRobot_DFPlayer_Mini1.SPK_2, SP1.+
  N5: S1.leg1, VCC1.-
